# Fritzing sketch GPSPotHoleTrack_Squematics (saved by Fritzing 0.9.3b)

parts:
  Componente1 = Flora GPS
  Componente2 = Adafruit Flora [part_number="Adafruit #659"]
  Componente3 = LilyPad Button Board
  Componente4 = LilyPad Button Board  # not connected
  Componente5 = LilyPad Button Board  # not connected
  Componente6 = LilyPad Button Board  # not connected
  Componente7 = LilyPad Button Board
  Componente8 = I2C Non-Volatile FRAM 32KB
  BAT2 = Sewable CR2032 Battery Holder [package=battery_20mm_pth_compact]
  Componente9 = LilyPad Button Board
  Componente10 = LilyPad Buzzer

nets:
  3.3V: Componente1.3.3V, Componente2.+3V3, Componente8.VCC
  GND: Componente1.GND, Componente2.GND, Componente3.-, Componente7.-, BAT2.-, Componente9.-, Componente10.-
  N1: Componente1.RX, Componente2.IO1/TX
  N2: Componente1.BAT, BAT2.+
  N3: Componente1.TX, Componente2.IO0/RX
  N4: Componente2.IO6, Componente3.S
  N5: Componente2.IO9, Componente9.S
  N6: Componente2.IO10, Componente10.+
  N7: Componente2.IO12, Componente7.S
  N8: Componente2.IO2/SDA, Componente8.SCL
  N9: Componente2.IO3/SCL, Componente8.SDA

custom parts:
  Flora GPS: This module is the best way to add a GPS to your wearable project. It's part of the Adafruit Flora series of wearable electronics, designed specifically for use with the Flora motherboard. Installed on the PCB is the latest of our Ultimate GPS modules, a small, super-thin, low power GPS module with built in data-logging capability!
  Adafruit Flora: FLORA is Adafruit's fully-featured wearable electronics platform. It's a round, sewable, Arduino-compatible microcontroller designed to empower amazing wearables projects. The FLORA is small (1.75" diameter, weighing 4.4 grams). The FLORA has built-in USB support. Built in USB means you plug it in to program it, it just shows up - all you need is a Micro-B USB cable, no additional purchases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
  I2C Non-Volatile FRAM 32KB: With our I2C FRAM breakout board you can add some FRAM storage to your next DIY project. FRAM allows for a lower power usage and a faster write performance. It's excellent for low-power or inconsistent-power datalogging or data buffering where you want to stream data fast while also keeping the data when there's no power. Unlike Flash or EEPROM there's no pages to worry about. Each byte can be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
  Sewable CR2032 Battery Holder: Battery Holders Various common sizes : AA, AAA, 20mm coin cell and 12mm coin cell.
